# Fritzing sketch Sketch (saved by Fritzing 0.9.3b)
breadboards: 1

parts:
  Nano1 = Arduino Nano v2.3
  Bauteil1 = 24 NeoPixel Ring [part_number=1586]
  S1 = SWITCH-MOMENTARY-2 [package=tactile-pth]

nets:
  N1: Nano1.D1TX, S1.1
  N2: Nano1.A5, Bauteil1.IN
  +5V: Nano1.+5V, Bauteil1.VDD
  GND: Nano1.GND, Bauteil1.GND

custom parts:
  24 NeoPixel Ring: 24 ultra bright smart LED NeoPixels are arranged in a circle with 2.6" (66mm) outer diameter. The rings are 'chainable' - connect the output pin of one to the input pin of another. Use only one microcontroller pin to control as many as you can chain together! Each LED is addressable as the driver chip is inside the LED. Each one has ~18mA constant current drive so the color will be very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
